// Logisim project ALUFinalFinal.circ as structural Verilog: 1 circuit, main circuit main
module main (
  input  [3:0] A,
  input  [3:0] B,
  input  in_3,
  input  in_4,
  input  in_5,
  output [3:0] E,
  output Z,
  output V
);

  wire and_5_out, and_6_out, and_7_out, and_8_out, and_9_out, and_10_out, and_11_out, and_12_out, and_13_out,
       and_14_out, and_15_out, and_16_out, or_5_out, or_6_out, or_7_out, or_8_out, or_9_out, xor_1_out,
       xor_2_out, xor_3_out, xor_4_out, xor_13_out, xor_14_out, xor_15_out, xor_16_out;
  wire [3:0] and_1_out, not_1_out, or_1_out, xor_5_out, xor_9_out, xor_17_out;

  xor xor_1 (xor_1_out, in_3, B[0]);
  xor xor_2 (xor_2_out, in_3, B[1]);
  xor xor_3 (xor_3_out, in_3, B[2]);
  xor xor_4 (xor_4_out, in_3, B[3]);
  and and_1 (and_1_out[0], A[0], B[0]);
  and and_2 (and_1_out[1], A[1], B[1]);
  and and_3 (and_1_out[2], A[2], B[2]);
  and and_4 (and_1_out[3], A[3], B[3]);
  or or_1 (or_1_out[0], A[0], B[0]);
  or or_2 (or_1_out[1], A[1], B[1]);
  or or_3 (or_1_out[2], A[2], B[2]);
  or or_4 (or_1_out[3], A[3], B[3]);
  xor xor_5 (xor_5_out[0], A[0], B[0]);
  xor xor_6 (xor_5_out[1], A[1], B[1]);
  xor xor_7 (xor_5_out[2], A[2], B[2]);
  xor xor_8 (xor_5_out[3], A[3], B[3]);
  not not_1 (not_1_out[0], B[0]);
  not not_2 (not_1_out[1], B[1]);
  not not_3 (not_1_out[2], B[2]);
  not not_4 (not_1_out[3], B[3]);
  xor xor_9 (xor_9_out[0], 1'b1, B[0]);
  xor xor_10 (xor_9_out[1], and_8_out, B[1]);
  and and_5 (and_5_out, and_8_out, B[1]);
  xor xor_11 (xor_9_out[2], and_5_out, B[2]);
  and and_6 (and_6_out, and_5_out, B[2]);
  xor xor_12 (xor_9_out[3], and_6_out, B[3]);
  and and_7 (and_7_out, and_6_out, B[3]);
  and and_8 (and_8_out, 1'b1, B[0]);
  xor xor_13 (xor_13_out, A[0], xor_1_out);
  xor xor_14 (xor_14_out, xor_2_out, A[1]);
  and and_9 (and_9_out, xor_2_out, A[1]);
  xor xor_15 (xor_15_out, xor_3_out, A[2]);
  and and_10 (and_10_out, xor_3_out, A[2]);
  xor xor_16 (xor_16_out, xor_4_out, A[3]);
  and and_11 (and_11_out, xor_4_out, A[3]);
  and and_12 (and_12_out, A[0], xor_1_out);
  and and_13 (and_13_out, xor_15_out, or_6_out);
  and and_14 (and_14_out, xor_16_out, or_7_out);
  xor xor_17 (xor_17_out[0], xor_13_out, in_3);
  and and_15 (and_15_out, xor_13_out, in_3);
  xor xor_18 (xor_17_out[1], xor_14_out, or_5_out);
  and and_16 (and_16_out, xor_14_out, or_5_out);
  xor xor_19 (xor_17_out[2], xor_15_out, or_6_out);
  xor xor_20 (xor_17_out[3], xor_16_out, or_7_out);
  or or_5 (or_5_out, and_15_out, and_12_out);
  or or_6 (or_6_out, and_16_out, and_9_out);
  or or_7 (or_7_out, and_13_out, and_10_out);
  or or_8 (or_8_out, and_14_out, and_11_out);
  Multiplexer multiplexer_1 (.in0(or_8_out), .in1(and_7_out), .out(V), .sel(in_5));
  Multiplexer #(.select(3), .width(4)) multiplexer_2 (
    .in0(xor_17_out), .in1(xor_17_out), .in2(and_1_out), .in3(or_1_out), .in4(xor_5_out), .in5(not_1_out),
    .in6(xor_9_out), .in7({{2{B[3]}}, B[2:1]}), .out(E), .sel({in_5, in_4, in_3}));
  or or_9 (or_9_out, E[0], E[1], E[2], E[3]);
  not not_5 (Z, or_9_out);

  // Notes on the sheet:
  //   Increment, 4 half adders with a power line connected so it can add 1
  //   The logic unit, AND OR XOR NOT 
  //   Full Adder With subtract capabilities
  //   This wire is connected to the MUX input line S0, so once the user selects 001, it activates subtraction
  //   The Carry out of the full adder, connected in an OR gate with the increment carry out, so it can activate the overflow flag
  //   The V flag that indicates an overflow, two inputs are the carry out signals from the full adder and the increment
  //   The MUX select line, S0, S1, S2, from top to bottom
  //   The Z flag that should equal 1 if the input is zero
endmodule
